# Fritzing sketch ReceiptPaperGame (saved by Fritzing 1.0.5)
breadboards: 1

parts:
  Pico/Pico2_Mod_1 = Raspberry Pi Pico or Pico 2
  Part2 = I2C level shifter bidirectional
  S1 = Momentary Switch [package=ksa_sealed_tac_switch]
  Part3 = 12 NeoPixel Ring [part_number=1643]
  Part4 = 16 NeoPixel Ring [part_number=1463]
  Part5 = 24 NeoPixel Ring [part_number=1586]
  S2 = Round Pushbutton
  S3 = Round Pushbutton
  S4 = Round Pushbutton
  S5 = Round Pushbutton
  S6 = Round Pushbutton
  Part6 = Thermal Printer
  JACK1 = 2.1mm Barrel Jack with Terminal Block

nets:
  GND: Pico/Pico2_Mod_1.pin_3, Pico/Pico2_Mod_1.pin_8, Pico/Pico2_Mod_1.pin_13, Pico/Pico2_Mod_1.pin_18, Pico/Pico2_Mod_1.pin_23, Pico/Pico2_Mod_1.pin_28, Pico/Pico2_Mod_1.pin_33, Pico/Pico2_Mod_1.pin_38, Pico/Pico2_Mod_1.pin_42, Part2.GND, S1.1, Part3.GND, Part4.GND, Part5.GND, S2.leg1, S3.leg1, S4.leg1, S5.leg1, S6.leg1
  N1: Pico/Pico2_Mod_1.pin_4, Part2.LV1
  N2: Pico/Pico2_Mod_1.pin_5, Part2.LV2
  N3: Pico/Pico2_Mod_1.pin_6, Part2.LV3
  N4: Pico/Pico2_Mod_1.pin_22, S6.leg0
  N5: Pico/Pico2_Mod_1.pin_24, S2.leg0
  N6: Pico/Pico2_Mod_1.pin_25, S5.leg0
  N7: Pico/Pico2_Mod_1.pin_26, S4.leg0
  N8: Pico/Pico2_Mod_1.pin_27, S3.leg0
  N9: Pico/Pico2_Mod_1.pin_30, S1.3
  N10: Pico/Pico2_Mod_1.pin_37, Part2.LV
  VDD: Pico/Pico2_Mod_1.pin_39, Part2.HV, Part3.VDD, Part4.VDD, Part5.VDD
  N11: Part2.HV1, Part3.IN
  N12: Part2.HV2, Part4.IN
  N13: Part2.HV3, Part5.IN
  N14: Part6.GND#0, JACK1.NEG
  N15: Part6.VH, JACK1.POS

custom parts:
  Raspberry Pi Pico or Pico 2: Raspberry Pi Pico and Pico 2. Based around the RP2040 and RP2350 microcontrollers respectively, Picos are low cost microcontroller device bringing Raspberry Pi quality, cost, and easy of use to the microcontroller space. Jan 2021, Split part in to two versions: tht (this one) and SMD. This one will drill holes for a .1 in header in pcb to allow plugging in the module as well as providing pads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
  12 NeoPixel Ring: 12 ultra bright smart LED NeoPixels are arranged in a circle with 1.5" (37mm) outer diameter. The rings are 'chainable' - connect the output pin of one to the input pin of another. Use only one microcontroller pin to control as many as you can chain together! Each LED is addressable as the driver chip is inside the LED. Each one has ~18mA constant current drive so the color will be very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
  16 NeoPixel Ring: 16 ultra bright smart LED NeoPixels are arranged in a circle with 1.75" (44.5mm) outer diameter. The rings are 'chainable' - connect the output pin of one to the input pin of another. Use only one microcontroller pin to control as many as you can chain together! Each LED is addressable as the driver chip is inside the LED. Each one has ~18mA constant current drive so the color will be very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
  24 NeoPixel Ring: 24 ultra bright smart LED NeoPixels are arranged in a circle with 2.6" (66mm) outer diameter. The rings are 'chainable' - connect the output pin of one to the input pin of another. Use only one microcontroller pin to control as many as you can chain together! Each LED is addressable as the driver chip is inside the LED. Each one has ~18mA constant current drive so the color will be very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
